# Fritzing sketch Sketch (saved by Fritzing 1.0.4)
breadboards: 1

parts:
  microSD1 = MicroSD Card Module
  S1 = Momentary Switch [package=ksa_sealed_tac_switch]
  R1 = Resistor [tolerance=±5% resistance=100k package="0603 [SMD]"]
  R2 = Resistor [tolerance=±5% resistance=100k package="0603 [SMD]"]
  U1 = LIPO-2000mAh [package=lipo-2000]
  U2 = ESP32S-HiLetgo [part_number=ESP32S-HiLetgo]

nets:
  GND: microSD1.GND, S1.2, U2.GND
  N1: microSD1.VCC, U2.3.3
  N2: microSD1.MISO, U2.GPIO22
  N3: microSD1.MOSI, U2.GPIO23
  N4: microSD1.SCK, U2.GPIO18
  N5: microSD1.CS, U2.GPIO17
  N6: S1.3, U2.EN
  N7: R1.Pin_0, U1.+
  N8: R1.Pin_1, R2.Pin_0, U2.GPIO34
  N9: R2.Pin_1, U1.-

custom parts:
  ESP32S-HiLetgo: HiLetgo ESP-WROOM-32 ESP32 ESP-32S Development Board 2.4GHz Dual-Mode WiFi + Bluetooth Dual Cores Microcontroller The ESP32 integrated with Antenna switches, RF Balun, power amplifiers, low-noise amplifiers, filters, and management modules, and the entire solution occupies the least area of PCB. 2.4 GHz Wi-Fi plus Bluetooth dual-mode chip, with TSMC Ultra-low power consumption 40nm technology,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
